# Fritzing sketch pcb-pi (saved by Fritzing 0.9.2b)
circuit board: 6.52901cm x 5.61683cm
breadboards: 1

parts:
  U2 = mystery part, 24 pins [chip_label=?]
  J1 = male pin header, 3 pins [form="♂ (male)"]
  J2 = male pin header, 3 pins [form="♂ (male)"]
  J3 = male pin header, 3 pins [form="♂ (male)"]
  J4 = male pin header, 3 pins [form="♂ (male)"]
  J5 = male pin header, 3 pins [form="♂ (male)"]
  J6 = male pin header, 3 pins [form="♂ (male)"]
  J7 = male pin header, 3 pins [form="♂ (male)"]
  J8 = male pin header, 3 pins [form="♂ (male)"]
  J9 = male pin header, 3 pins [form="♂ (male)"]
  J10 = male pin header, 3 pins [form="♂ (male)"]
  J11 = male pin header, 3 pins [form="♂ (male)"]
  J12 = male pin header, 3 pins [form="♂ (male)"]
  U1 = mystery part, 40 pins [chip_label=?]
  J13 = female pin header, 2 pins [form="♀ (female)"]
  on = mystery part, 6 pins [chip_label=?]
  +_- = mystery part, 4 pins [chip_label=?]
  R2 = Resistor [tolerance=±5% resistance=220 package="1206 [SMD]"]
  R1 = Resistor [tolerance=±5% resistance=220 package="1206 [SMD]"]
  R3 = Resistor [tolerance=±5% resistance=220 package="1206 [SMD]"]
  R4 = Resistor [tolerance=±5% resistance=220 package="1206 [SMD]"]
  C1 = Ceramic Capacitor [capacitance=100nF package="1206 [SMD, multilayer]"]
  reg = mystery part, 4 pins [chip_label=?]
  J14 = female pin header, 2 pins [form="♀ (female)"]
  tx_rx_2_3 = female pin header, 4 pins [form="♀ (female)"]

nets:
  N1: U2.pin1, tx_rx_2_3.pin4
  N2: U2.pin2, tx_rx_2_3.pin3
  N3: U2.pin5, tx_rx_2_3.pin2
  N4: U2.pin6, tx_rx_2_3.pin1
  N5: U2.pin7, J1.pin3
  N6: U2.pin8, J2.pin3
  N7: U2.pin9, J3.pin3
  N8: U2.pin10, J4.pin3
  N9: U2.pin11, J5.pin3
  N10: U2.pin12, J6.pin3
  N11: U2.pin13, J10.pin3
  N12: U2.pin14, J7.pin3
  N13: U2.pin15, J11.pin3
  N14: U2.pin16, J14.pin2
  N15: U2.pin17, J12.pin3
  N16: U2.pin18, J8.pin3
  N17: U2.pin19, J9.pin3
  N18: U2.pin20, R3.Pin_0, R4.Pin_0, C1.0
  N19: U2.pin23, J1.pin1, J2.pin1, J3.pin1, J4.pin1, J5.pin1, J6.pin1, J7.pin1, J8.pin1, J9.pin1, J10.pin1, J11.pin1, J12.pin1, U1.pin4, +_-.pin1, +_-.pin4, reg.pin1, reg.pin4, J14.pin1
  N20: U2.pin24, J1.pin2, J2.pin2, J3.pin2, J4.pin2, J5.pin2, J6.pin2, J7.pin2, J8.pin2, J9.pin2, J10.pin2, J11.pin2, J12.pin2, U1.pin39, U1.pin40, reg.pin2
  N21: U1.pin2, J13.pin2, R1.Pin_0
  N22: U1.pin3, J13.pin1, R2.Pin_0
  N23: U1.pin8, R2.Pin_1, R1.Pin_1
  N24: U1.pin12, R4.Pin_1, C1.1
  N25: on.pin1, on.pin2, on.pin5, on.pin6, R3.Pin_1, reg.pin3
  N26: on.pin3, on.pin4, +_-.pin2, +_-.pin3
