# Fritzing sketch pcb4 (saved by Fritzing 0.9.2b)
circuit board: 4.95cm x 4.95cm
breadboards: 1

parts:
  Part1 = Arduino Pro Mini v13
  U1 = mystery part, 3 pins [chip_label=?]
  U2 = mystery part, 3 pins [chip_label=?]
  U3 = mystery part, 3 pins [chip_label=?]
  U4 = mystery part, 3 pins [chip_label=?]
  U5 = mystery part, 3 pins [chip_label=?]
  U6 = mystery part, 3 pins [chip_label=?]
  U7 = mystery part, 3 pins [chip_label=?]
  U8 = mystery part, 3 pins [chip_label=?]
  U9 = mystery part, 3 pins [chip_label=?]
  U10 = mystery part, 3 pins [chip_label=?]
  U11 = mystery part, 3 pins [chip_label=?]
  U12 = mystery part, 3 pins [chip_label=?]
  47kΩ = Resistor [tolerance=±5% resistance=220 package="1206 [SMD]"]
  47kΩ_2 = Resistor [tolerance=±5% resistance=220 package="1206 [SMD]"]
  47nF = Ceramic Capacitor [capacitance=100nF package="1206 [SMD, multilayer]"]
  power_on = double row female pin header, 6 pins [form="♀ (female)"]
  +bat- = double row female pin header, 4 pins [form="♀ (female)"]
  ---B = female pin header, 2 pins [form="♀ (female)"]
  ---A = female pin header, 2 pins [form="♀ (female)"]
  1000µF = Electrolytic Capacitor [capacitance=1µF package="200 mil [THT, electrolytic]"]
  A6_A7 = female pin header, 2 pins [form="♀ (female)"]
  J2 = female pin header, 2 pins [form="♀ (female)"]
  3 = mystery part, 4 pins [chip_label=?]
  2 = mystery part, 4 pins [chip_label=?]
  A5 = mystery part, 4 pins [chip_label=?]
  A4 = mystery part, 4 pins [chip_label=?]
  13 = mystery part, 4 pins [chip_label=?]
  A6 = mystery part, 4 pins [chip_label=?]
  A7 = mystery part, 4 pins [chip_label=?]
  rx_tx = female pin header, 2 pins [form="♀ (female)"]
  J3 = double row female pin header, 6 pins [form="♀ (female)"]  # not connected

nets:
  N1: Part1.VCC, 3.pin4, 2.pin4, A5.pin4, A4.pin4, 13.pin4, A6.pin4, A7.pin4
  N2: Part1.GND, U1.pin1, U2.pin1, U3.pin1, U4.pin1, U5.pin1, U6.pin1, U7.pin1, U8.pin1, U9.pin1, U10.pin1, U11.pin1, U12.pin1, 47kΩ.Pin_1, 47nF.1, +bat-.pin1, +bat-.pin2, 1000µF.-, 3.pin1, 2.pin1, A5.pin1, A4.pin1, 13.pin1, A6.pin1, A7.pin1
  N3: Part1.A4, A4.pin3
  N4: Part1.A5, A5.pin3
  N5: Part1.RAW, U1.pin2, U2.pin2, U3.pin2, U4.pin2, U5.pin2, U6.pin2, U7.pin2, U8.pin2, U9.pin2, U10.pin2, U11.pin2, U12.pin2, 47kΩ_2.Pin_1, power_on.pin1, power_on.pin6, ---B.pin1, ---B.pin2, ---A.pin1, ---A.pin2, 1000µF.+, 3.pin2, 2.pin2, A5.pin2, A4.pin2, 13.pin2, A6.pin2, A7.pin2
  N6: Part1.A3, 47kΩ.Pin_0, 47kΩ_2.Pin_0, 47nF.0
  N7: Part1.A2, U1.pin3
  N8: Part1.A1, U2.pin3
  N9: Part1.A0, U3.pin3
  N10: Part1.D13/SCK, 13.pin3
  N11: Part1.D12/MISO, U4.pin3
  N12: Part1.D11_PWM/MOSI, U5.pin3
  N13: Part1.D10_PWM/SS, U6.pin3
  N14: Part1.D9_PWM, U7.pin3
  N15: Part1.D8, U10.pin3
  N16: Part1.D7, U9.pin3
  N17: Part1.D6_PWM, U11.pin3
  N18: Part1.D5_PWM, U12.pin3
  N19: Part1.D4, U8.pin3
  N20: Part1.D3_PWM, 3.pin3
  N21: Part1.D2, 2.pin3
  N22: Part1.D1/RX, rx_tx.pin2
  N23: Part1.D0/TX, rx_tx.pin1
  N24: power_on.pin2, power_on.pin3, power_on.pin4, power_on.pin5, +bat-.pin3, +bat-.pin4
  N25: A6_A7.pin1, J2.pin1, A7.pin3
  N26: A6_A7.pin2, J2.pin2, A6.pin3

notes:
  3V3 * GND RAW
